// Logisim project Buffer.circ as structural Verilog: 1 circuit, main circuit main
module main (
  input  [7:0] INPUT___IN,
  input  IN_BUS,
  input  BUS_A,
  input  REG_A_GAT,
  input  BUS_B,
  input  REG_B_GAT,
  input  BUS_C,
  input  REG_C_GAT
);

  wire [7:0] controlled_buffer_1_out, REG_A_q, REG_B_q, REG_C_q;

  assign controlled_buffer_1_out = IN_BUS ? INPUT___IN : 8'bz;  // Controlled_Buffer controlled_buffer_1
  Register REG_A (.D(controlled_buffer_1_out), .Q(REG_A_q), .clk(REG_A_GAT));  // open: en, clr
  Register REG_B (.D(controlled_buffer_1_out), .Q(REG_B_q), .clk(REG_B_GAT));  // open: en, clr
  Register REG_C (.D(controlled_buffer_1_out), .Q(REG_C_q), .clk(REG_C_GAT));  // open: en, clr
  assign controlled_buffer_1_out = BUS_A ? REG_A_q : 8'bz;  // Controlled_Buffer controlled_buffer_2
  assign controlled_buffer_1_out = BUS_B ? REG_B_q : 8'bz;  // Controlled_Buffer controlled_buffer_3
  assign controlled_buffer_1_out = BUS_C ? REG_C_q : 8'bz;  // Controlled_Buffer controlled_buffer_4
endmodule
