// Logisim project Decodificador.circ as structural Verilog: 1 circuit, main circuit main
// DEC
module main (
  input  [3:0] in_1,
  output LOAD,
  output FETCH,
  output HALT,
  output NOP,
  output STORE,
  output ADD,
  output COMP
);

  and and_1 (LOAD, ~in_1[3], ~in_1[2], ~in_1[1], in_1[0]);  // AND_Gate
  and and_2 (FETCH, ~in_1[3], ~in_1[2], ~in_1[1], ~in_1[0]);  // AND_Gate
  and and_3 (HALT, ~in_1[3], in_1[2], ~in_1[1], in_1[0]);  // AND_Gate
  and and_4 (NOP, in_1[3], in_1[2], in_1[1], in_1[0]);
  and and_5 (STORE, ~in_1[3], ~in_1[2], in_1[1], in_1[0]);  // AND_Gate
  and and_6 (ADD, ~in_1[3], ~in_1[2], in_1[1], ~in_1[0]);  // AND_Gate
  and and_7 (COMP, ~in_1[3], in_1[2], ~in_1[1], ~in_1[0]);  // AND_Gate
endmodule
