// Logisim project Flip flop.circ as structural Verilog: 1 circuit, main circuit main
module main (
  input  D3,
  input  D2,
  input  D1,
  input  D0,
  input  ENABLE,
  input  Reset,
  output S3,
  output S2,
  output S1,
  output S0
);

  wire clock_1_out;

  Clock clock_1 (.out(clock_1_out));
  D_Flip_Flop d_ff_1 (.clk(clock_1_out), .D(D3), .Q(S3), .preset(ENABLE), .en(ENABLE), .reset(ENABLE));  // open: Qn
  D_Flip_Flop d_ff_2 (.clk(clock_1_out), .D(D2), .Q(S2), .en(ENABLE), .reset(ENABLE));  // open: Qn, preset
  D_Flip_Flop d_ff_3 (.clk(clock_1_out), .D(D1), .Q(S1), .en(ENABLE), .reset(ENABLE));  // open: Qn, preset
  D_Flip_Flop #(.trigger("falling")) d_ff_4 (.clk(clock_1_out), .D(D0), .Q(S0));  // open: Qn, preset, en, reset

  assign Reset = ENABLE;
endmodule
