// Logisim project Latch-D-4bits.circ as structural Verilog: 1 circuit, main circuit main
module main (
  input  CLOCK,
  input  D3,
  input  D2,
  input  D1,
  input  D0,
  input  ENABLE,
  input  RESET,
  output S3,
  output S2,
  output S1,
  output S0
);

  wire clock_1_out;

  Clock clock_1 (.out(clock_1_out));
  D_Flip_Flop d_ff_1 (.clk(clock_1_out), .D(D3), .Q(S3), .en(ENABLE), .reset(RESET));  // open: Qn, preset
  D_Flip_Flop d_ff_2 (.clk(clock_1_out), .D(D2), .Q(S2), .en(ENABLE), .reset(RESET));  // open: Qn, preset
  D_Flip_Flop d_ff_3 (.clk(clock_1_out), .D(D1), .Q(S1), .en(ENABLE), .reset(RESET));  // open: Qn, preset
  D_Flip_Flop d_ff_4 (.clk(clock_1_out), .D(D0), .Q(S0), .en(ENABLE), .reset(RESET));  // open: Qn, preset
endmodule
