// Logisim project RAM.circ as structural Verilog: 1 circuit, main circuit main
module main (
  input  RDM_GAT,
  input  RAM_GAT,
  input  RAM_GAT_2,
  input  RAM_BUS,
  input  [7:0] INPUT___IN,
  input  REG_IN_GAT,
  input  REG_IN_BUS,
  input  RI_GAT,
  output [7:0] out_9
);

  wire [7:0] ram_1_data, RDM_q, REG_IN_q, REM_q;

  Register REM (.D(ram_1_data), .Q(REM_q), .clk(RAM_GAT));  // open: en, clr
  Register REG_IN (.D(INPUT___IN), .Q(REG_IN_q), .clk(REG_IN_GAT));  // open: en, clr
  RAM ram_1 (.addr(REM_q), .data(ram_1_data), .clk(RAM_GAT_2), .ld(RAM_BUS));  // open: sel, clr
  assign ram_1_data = REG_IN_BUS ? REG_IN_q : 8'bz;  // Controlled_Buffer controlled_buffer_1
  Register RDM (.D(ram_1_data), .Q(RDM_q), .clk(RDM_GAT));  // open: en, clr
  Register RI (.D(RDM_q), .Q(out_9), .clk(RI_GAT));  // open: en, clr

  // Notes on the sheet:
  //   RAM
  //   vai pra unidade de controle
endmodule
