// Logisim project Registrador.circ as structural Verilog: 1 circuit, main circuit main
module main (
  input  [9:0] INPUT,
  input  ENABLE,
  input  CLK_A,
  input  CLK_B,
  input  in_5,
  output [9:0] OUTPUT
);

  wire [9:0] COMP_A_q;

  Register #(.width(10)) COMP_A (.D(INPUT), .en(ENABLE), .Q(COMP_A_q), .clk(CLK_A), .clr(in_5));
  Register #(.width(10)) COMP_B (.D(COMP_A_q), .en(ENABLE), .Q(OUTPUT), .clk(CLK_B), .clr(in_5));
endmodule
