// Logisim project contador de programa.circ as structural Verilog: 1 circuit, main circuit main
module main (
  input  PC_GATILHO,
  input  LIMPAR_PC,
  output [7:0] out_3
);

  wire clock_1_out;
  wire [7:0] adder_1_out;

  Adder adder_1 (.a(out_3), .b(8'h1), .out(adder_1_out));  // open: cin, cout
  Clock clock_1 (.out(clock_1_out));
  Register PC (.D(adder_1_out), .Q(out_3), .clr(LIMPAR_PC));  // open: en, clk

  // Notes on the sheet:
  //   CONTADOR DE PROGRAMA - PC - (PROGRAM COUNTER)
endmodule
