// Logisim project 4_comp2b.circ as structural Verilog: 1 circuit, main circuit 4_comp2b
// COMP2b
module _4_comp2b (
  input  A,
  input  B,
  input  ANT_A_MAIOR_B,
  input  ANT_A_IGUAL_B,
  input  ANT_B_MAIOR_A,
  output A_MAIOR_B,
  output A_IGUAL_B,
  output B_MAIOR_A
);

  wire and_1_out, and_2_out, and_3_out, and_4_out, and_5_out, and_6_out, not_1_out, not_2_out, not_3_out,
       not_4_out, not_5_out;

  not not_1 (not_1_out, A);
  not not_2 (not_2_out, B);
  not not_3 (not_3_out, ANT_A_MAIOR_B);
  not not_4 (not_4_out, ANT_A_IGUAL_B);
  not not_5 (not_5_out, ANT_B_MAIOR_A);
  and and_1 (and_1_out, ANT_A_MAIOR_B, not_4_out, not_5_out);
  and and_2 (and_2_out, A, not_2_out, not_3_out, ANT_A_IGUAL_B, not_5_out);
  and and_3 (and_3_out, not_1_out, not_2_out, not_3_out, ANT_A_IGUAL_B, not_5_out);
  and and_4 (and_4_out, A, B, not_3_out, ANT_A_IGUAL_B, not_5_out);
  and and_5 (and_5_out, not_1_out, B, not_3_out, ANT_A_IGUAL_B, not_5_out);
  and and_6 (and_6_out, not_3_out, not_4_out, ANT_B_MAIOR_A);
  or or_1 (A_MAIOR_B, and_1_out, and_2_out);
  or or_2 (A_IGUAL_B, and_3_out, and_4_out);
  or or_3 (B_MAIOR_A, and_5_out, and_6_out);
endmodule
