// Logisim project 5_ula.circ as structural Verilog: 1 circuit, main circuit ULA
module ULA (
  input  [7:0] ACC_IN,
  input  ADD_TG,
  input  [7:0] INPUT,
  input  ULA_TG,
  input  COMP_TG,
  input  [1:0] SELETOR_DA_OPERACAO,
  output [7:0] ACC_OUT,
  output A_MAIOR_B,
  output IGUAIS,
  output B_MAIOR_A
);

  wire and_1_out, not_1_out;
  wire [7:0] adder_1_out, COMP_q, demultiplexer_1_out1, demultiplexer_1_out2;

  Demultiplexer #(.select(2), .width(8)) demultiplexer_1 (
    .out1(demultiplexer_1_out1), .out2(demultiplexer_1_out2), .in(INPUT), .sel(SELETOR_DA_OPERACAO),
    .en(ULA_TG));  // open: out0, out3
  not not_1 (not_1_out, SELETOR_DA_OPERACAO[0]);
  and and_1 (and_1_out, SELETOR_DA_OPERACAO[1], not_1_out, COMP_TG);
  Adder adder_1 (.a(ACC_IN), .b(demultiplexer_1_out1), .out(adder_1_out));  // open: cin, cout
  Register ADD (.D(adder_1_out), .Q(ACC_OUT), .clk(ADD_TG));  // open: en, clr
  Register COMP (.D(demultiplexer_1_out2), .Q(COMP_q), .clk(COMP_TG));  // open: en, clr
  CMP cmp_1 (
    .ENABLE(and_1_out), .A7(ACC_IN[7]), .A6(ACC_IN[6]), .A5(ACC_IN[5]), .A4(ACC_IN[4]), .A3(ACC_IN[3]),
    .A2(ACC_IN[2]), .A1(ACC_IN[1]), .A0(ACC_IN[0]), .B7(COMP_q[7]), .B6(COMP_q[6]), .B5(COMP_q[5]),
    .B4(COMP_q[4]), .B3(COMP_q[3]), .B2(COMP_q[2]), .B1(COMP_q[1]), .B0(COMP_q[0]), .\A_É_MAIOR (A_MAIOR_B),
    .IGUAIS(IGUAIS), .\B_É_MAIOR (B_MAIOR_A));

  // Notes on the sheet:
  //   "vem da UC"
  //   Segunda variável "Y"
  //   Primeira variável "X"
  //   SOMA (01)
  //   COMPARAÇÃO (10)
  //   ULA - UNIDADE LÓGICA E ARITMÉTICA (SOMA E COMPARAÇÃO)
endmodule
