// Logisim project 6_uc.circ as structural Verilog: 1 circuit, main circuit UC
module UC (
  input  [7:0] INPUT,
  output [7:0] \ENDEREÇO ,
  output [1:0] OPERACAO
);

  wire n2_dec_1_fetch_busca, \n2_dec_1_halt_término , n2_dec_1_load_leitura, \n2_dec_1_nop_sem_operação ,
       n2_dec_1_store_escrita;
  wire [17:0] rom_1_data;

  _2_dec u_2_dec_1 (
    .INPUT(INPUT[7:4]), .FETCH_BUSCA(n2_dec_1_fetch_busca), .LOAD_LEITURA(n2_dec_1_load_leitura),
    .ADD_SOMA(OPERACAO[0]), .\COMP_COMPARAÇÃO (OPERACAO[1]), .STORE_ESCRITA(n2_dec_1_store_escrita),
    .\NOP_SEM_OPERAÇÃO (\n2_dec_1_nop_sem_operação ), .\HALT_TÉRMINO (\n2_dec_1_halt_término ));
  ROM #(.dataWidth(18)) rom_1 (.data(rom_1_data));  // open: addr, sel
  LED HALT (.in(\n2_dec_1_halt_término ));
  LED NOP (.in(\n2_dec_1_nop_sem_operação ));
  LED FECTH (.in(n2_dec_1_fetch_busca));
  LED STORE (.in(n2_dec_1_store_escrita));
  LED LOAD (.in(n2_dec_1_load_leitura));
  LED COMP (.in(OPERACAO[1]));
  LED ADD (.in(OPERACAO[0]));

  assign \ENDEREÇO  = {4'b0000, INPUT[3:0]};

  // Notes on the sheet:
  //   INSTRUÇÃO
  //   OBJETIVO: MEMÓRIA ROM MICROPROGRAMADA
  //   UNIDADE DE CONTROLE
  //   SEM MICROPROGRAMAÇÃO
  //   SINAIS DE CONTROLE - MICROINSTRUÇÕES
  //   01 = SOMA
  //   10 = COMPARAÇÃO
  //   -> vai para a ULA
endmodule
