// Logisim project 8_cpu.circ as structural Verilog: 1 circuit, main circuit main
module main (
  input  PC_BUS,
  input  PC_TG,
  input  PC_CLEAR,
  input  REM_TG,
  input  RDM_TG,
  input  RDM_BUS,
  input  RAM_TG,
  input  RAM_BUS,
  input  ACC_BUS,
  input  RI_TG,
  input  ULA_BUS,
  input  ACC_CLEAR,
  input  ACC_TG,
  input  UC_BUS,
  input  ULA_TG,
  input  COMP_TG,
  input  ADD_TG,
  output [7:0] ACC_OUT
);

  wire ula_1_a_maior_b, ula_1_b_maior_a, ula_1_iguais;
  wire [1:0] uc_1_operacao;
  wire [7:0] controlled_buffer_1_out, controlled_buffer_3_out, n1_pc_1_contador, ram_1_data, RDM_q, REM_q,
       RI_q, \uc_1_endereço , ula_1_acc_out;

  assign controlled_buffer_1_out = UC_BUS ? \uc_1_endereço  : 8'bz;  // Controlled_Buffer controlled_buffer_1
  _1_pc u_1_pc_1 (.PC_TG(PC_TG), .PC_CLEAR(PC_CLEAR), .CONTADOR(n1_pc_1_contador));
  Register RI (.D(controlled_buffer_3_out), .Q(RI_q), .clk(RI_TG));  // open: en, clr
  assign controlled_buffer_1_out = PC_BUS ? n1_pc_1_contador : 8'bz;  // Controlled_Buffer controlled_buffer_2
  UC uc_1 (.INPUT(RI_q), .\ENDEREÇO (\uc_1_endereço ), .OPERACAO(uc_1_operacao));
  ULA ula_1 (
    .ACC_IN(ACC_OUT), .INPUT(controlled_buffer_3_out), .ACC_OUT(ula_1_acc_out), .A_MAIOR_B(ula_1_a_maior_b),
    .IGUAIS(ula_1_iguais), .B_MAIOR_A(ula_1_b_maior_a), .ULA_TG(ULA_TG), .SELETOR_DA_OPERACAO(uc_1_operacao),
    .ADD_TG(ADD_TG), .COMP_TG(COMP_TG));
  Register REM (.D(controlled_buffer_1_out), .Q(REM_q), .clk(REM_TG));  // open: en, clr
  LED A_MAIOR_B (.in(ula_1_a_maior_b));
  LED IGUAIS (.in(ula_1_iguais));
  LED B_MAIOR_A (.in(ula_1_b_maior_a));
  RAM ram_1 (.addr(REM_q), .data(ram_1_data), .clk(RAM_TG), .ld(RAM_BUS));  // open: sel, clr
  assign controlled_buffer_3_out = ULA_BUS ? ula_1_acc_out : 8'bz;  // Controlled_Buffer controlled_buffer_3
  Register RDM (.D(ram_1_data), .Q(RDM_q), .clk(RDM_TG));  // open: en, clr
  assign controlled_buffer_3_out = RDM_BUS ? RDM_q : 8'bz;  // Controlled_Buffer controlled_buffer_4
  _3_acc u_3_acc_1 (.IN(controlled_buffer_3_out), .ACC_TG(ACC_TG), .ACC_CLEAR(ACC_CLEAR), .ACC_OUT(ACC_OUT));
  assign ram_1_data = ACC_BUS ? ACC_OUT : 8'bz;  // Controlled_Buffer controlled_buffer_5

  // Notes on the sheet:
  //   ARQUITETURA DE COMPUTADORES - CPU TOLEDO v1.0 - MANUAL
  //   MEMÓRIA RAM
endmodule
