// Logisim project 1_pc.circ as structural Verilog: 1 circuit, main circuit 1_pc
// PC
module _1_pc (
  input  PC_TG,
  input  PC_CLEAR,
  output [7:0] CONTADOR
);

  wire [7:0] adder_1_out;

  Adder adder_1 (.a(CONTADOR), .b(8'h1), .out(adder_1_out));  // open: cin, cout
  Register PC (.D(adder_1_out), .Q(CONTADOR), .clk(PC_TG), .clr(PC_CLEAR));  // open: en

  // Notes on the sheet:
  //   PC - PROGRAM COUNTER
endmodule
