// Logisim project 4_comp8b.circ as structural Verilog: 1 circuit, main circuit 4_comp8b
// CMP
module _4_comp8b (
  input  A7,
  input  A6,
  input  A5,
  input  A4,
  input  A3,
  input  A2,
  input  A1,
  input  A0,
  input  B7,
  input  B6,
  input  B5,
  input  B4,
  input  B3,
  input  B2,
  input  B1,
  input  B0,
  input  ENABLE,
  output \A_É_MAIOR ,
  output IGUAIS,
  output \B_É_MAIOR 
);

  wire n4_comp2b_1_a_igual_b, n4_comp2b_1_a_maior_b, n4_comp2b_1_b_maior_a, n4_comp2b_2_a_igual_b,
       n4_comp2b_2_a_maior_b, n4_comp2b_2_b_maior_a, n4_comp2b_3_a_igual_b, n4_comp2b_3_a_maior_b,
       n4_comp2b_3_b_maior_a, n4_comp2b_4_a_igual_b, n4_comp2b_4_a_maior_b, n4_comp2b_4_b_maior_a,
       n4_comp2b_5_a_igual_b, n4_comp2b_5_a_maior_b, n4_comp2b_5_b_maior_a, n4_comp2b_6_a_igual_b,
       n4_comp2b_6_a_maior_b, n4_comp2b_6_b_maior_a, n4_comp2b_7_a_igual_b, n4_comp2b_7_a_maior_b,
       n4_comp2b_7_b_maior_a, n4_comp2b_8_a_igual_b, n4_comp2b_8_a_maior_b, n4_comp2b_8_b_maior_a;

  _4_comp2b u_4_comp2b_1 (
    .A(A7), .B(B7), .ANT_A_MAIOR_B(1'b0), .ANT_A_IGUAL_B(1'b1), .ANT_B_MAIOR_A(1'b0),
    .A_MAIOR_B(n4_comp2b_1_a_maior_b), .A_IGUAL_B(n4_comp2b_1_a_igual_b), .B_MAIOR_A(n4_comp2b_1_b_maior_a));
  _4_comp2b u_4_comp2b_2 (
    .A(A6), .B(B6), .ANT_A_MAIOR_B(n4_comp2b_1_a_maior_b), .ANT_A_IGUAL_B(n4_comp2b_1_a_igual_b),
    .ANT_B_MAIOR_A(n4_comp2b_1_b_maior_a), .A_MAIOR_B(n4_comp2b_2_a_maior_b),
    .A_IGUAL_B(n4_comp2b_2_a_igual_b), .B_MAIOR_A(n4_comp2b_2_b_maior_a));
  _4_comp2b u_4_comp2b_3 (
    .A(A5), .B(B5), .ANT_A_MAIOR_B(n4_comp2b_2_a_maior_b), .ANT_A_IGUAL_B(n4_comp2b_2_a_igual_b),
    .ANT_B_MAIOR_A(n4_comp2b_2_b_maior_a), .A_MAIOR_B(n4_comp2b_3_a_maior_b),
    .A_IGUAL_B(n4_comp2b_3_a_igual_b), .B_MAIOR_A(n4_comp2b_3_b_maior_a));
  _4_comp2b u_4_comp2b_4 (
    .A(A4), .B(B4), .ANT_A_MAIOR_B(n4_comp2b_3_a_maior_b), .ANT_A_IGUAL_B(n4_comp2b_3_a_igual_b),
    .ANT_B_MAIOR_A(n4_comp2b_3_b_maior_a), .A_MAIOR_B(n4_comp2b_4_a_maior_b),
    .A_IGUAL_B(n4_comp2b_4_a_igual_b), .B_MAIOR_A(n4_comp2b_4_b_maior_a));
  _4_comp2b u_4_comp2b_5 (
    .A(A3), .B(B3), .ANT_A_MAIOR_B(n4_comp2b_4_a_maior_b), .ANT_A_IGUAL_B(n4_comp2b_4_a_igual_b),
    .ANT_B_MAIOR_A(n4_comp2b_4_b_maior_a), .A_MAIOR_B(n4_comp2b_5_a_maior_b),
    .A_IGUAL_B(n4_comp2b_5_a_igual_b), .B_MAIOR_A(n4_comp2b_5_b_maior_a));
  _4_comp2b u_4_comp2b_6 (
    .A(A2), .B(B2), .ANT_A_MAIOR_B(n4_comp2b_5_a_maior_b), .ANT_A_IGUAL_B(n4_comp2b_5_a_igual_b),
    .ANT_B_MAIOR_A(n4_comp2b_5_b_maior_a), .A_MAIOR_B(n4_comp2b_6_a_maior_b),
    .A_IGUAL_B(n4_comp2b_6_a_igual_b), .B_MAIOR_A(n4_comp2b_6_b_maior_a));
  _4_comp2b u_4_comp2b_7 (
    .A(A1), .B(B1), .ANT_A_MAIOR_B(n4_comp2b_6_a_maior_b), .ANT_A_IGUAL_B(n4_comp2b_6_a_igual_b),
    .ANT_B_MAIOR_A(n4_comp2b_6_b_maior_a), .A_MAIOR_B(n4_comp2b_7_a_maior_b),
    .A_IGUAL_B(n4_comp2b_7_a_igual_b), .B_MAIOR_A(n4_comp2b_7_b_maior_a));
  _4_comp2b u_4_comp2b_8 (
    .A(A0), .B(B0), .ANT_A_MAIOR_B(n4_comp2b_7_a_maior_b), .ANT_A_IGUAL_B(n4_comp2b_7_a_igual_b),
    .ANT_B_MAIOR_A(n4_comp2b_7_b_maior_a), .A_MAIOR_B(n4_comp2b_8_a_maior_b),
    .A_IGUAL_B(n4_comp2b_8_a_igual_b), .B_MAIOR_A(n4_comp2b_8_b_maior_a));
  and and_1 (\A_É_MAIOR , ENABLE, n4_comp2b_8_a_maior_b);
  and and_2 (IGUAIS, ENABLE, n4_comp2b_8_a_igual_b);
  and and_3 (\B_É_MAIOR , n4_comp2b_8_b_maior_a, ENABLE);

  // Notes on the sheet:
  //   A
  //   B
  //   ANTERIOR
endmodule
