// Logisim project contador_por_intervalo.circ as structural Verilog: 1 circuit, main circuit CONT
module CONT (
  input  [7:0] MAXIMO,
  input  [7:0] MINIMO,
  input  CLOCK,
  output [7:0] VALOR_OUT
);

  wire comparator_1_eq, comparator_2_gt, comparator_3_eq, not_1_out, not_2_out, not_3_out;
  wire [7:0] adder_1_out, adder_2_out, controlled_buffer_1_out, controlled_buffer_3_out,
       controlled_buffer_5_out;

  assign controlled_buffer_1_out = not_1_out ? MINIMO : 8'bz;  // Controlled_Buffer controlled_buffer_1
  not not_1 (not_1_out, comparator_2_gt);
  assign controlled_buffer_1_out = comparator_2_gt ? adder_2_out : 8'bz;  // Controlled_Buffer controlled_buffer_2
  Comparator comparator_1 (.a(MINIMO), .b({8{1'b0}}), .eq(comparator_1_eq));  // open: gt, lt
  Adder adder_1 (.a({8{1'b0}}), .b(controlled_buffer_1_out), .out(adder_1_out));  // open: cin, cout
  assign controlled_buffer_3_out = not_2_out ? 8'h1 : 8'bz;  // Controlled_Buffer controlled_buffer_3
  not not_2 (not_2_out, comparator_1_eq);
  assign controlled_buffer_3_out = comparator_1_eq ? MINIMO : 8'bz;  // Controlled_Buffer controlled_buffer_4
  assign controlled_buffer_5_out = comparator_3_eq ? MINIMO : 8'bz;  // Controlled_Buffer controlled_buffer_5
  assign controlled_buffer_5_out = not_3_out ? adder_1_out : 8'bz;  // Controlled_Buffer controlled_buffer_6
  not not_3 (not_3_out, comparator_3_eq);
  Comparator comparator_2 (.a(adder_2_out), .b(controlled_buffer_3_out), .gt(comparator_2_gt));  // open: eq, lt
  Register register_1 (.D(controlled_buffer_5_out), .Q(VALOR_OUT), .clk(CLOCK));  // open: en, clr
  Comparator comparator_3 (.a(MAXIMO), .b(VALOR_OUT), .eq(comparator_3_eq));  // open: gt, lt
  Adder adder_2 (.a(VALOR_OUT), .b(8'h1), .out(adder_2_out));  // open: cin, cout

  // Notes on the sheet:
  //   CONTADOR BASEADO EM INTERVALO MÍNIMO E MÁXIMO
endmodule
