// Logisim project 6_uc.circ as structural Verilog: 1 circuit, main circuit 6_uc
// UC
module _6_uc (
  input  [7:0] INPUT,
  input  clock,
  output [7:0] \ENDEREÇO ,
  output [1:0] OPERACAO,
  output [17:0] out_5
);

  wire and_1_out, and_2_out, and_3_out, and_4_out, and_5_out, and_6_out, and_7_out, n2_dec_1_fetch_busca,
       \n2_dec_1_halt_término , n2_dec_1_load_leitura, \n2_dec_1_nop_sem_operação , n2_dec_1_store_escrita;
  wire [7:0] cont_1_valor_out, cont_2_valor_out, cont_3_valor_out, cont_4_valor_out, cont_5_valor_out,
       cont_6_valor_out, cont_7_valor_out, controlled_buffer_1_out;

  LED FETCH (.in(n2_dec_1_fetch_busca));
  LED LOAD (.in(n2_dec_1_load_leitura));
  LED ADD (.in(OPERACAO[0]));
  LED COMP (.in(OPERACAO[1]));
  LED STORE (.in(n2_dec_1_store_escrita));
  LED NOP (.in(\n2_dec_1_nop_sem_operação ));
  LED HALT (.in(\n2_dec_1_halt_término ));
  _2_dec u_2_dec_1 (
    .INPUT(INPUT[7:4]), .FETCH_BUSCA(n2_dec_1_fetch_busca), .LOAD_LEITURA(n2_dec_1_load_leitura),
    .ADD_SOMA(OPERACAO[0]), .\COMP_COMPARAÇÃO (OPERACAO[1]), .STORE_ESCRITA(n2_dec_1_store_escrita),
    .\NOP_SEM_OPERAÇÃO (\n2_dec_1_nop_sem_operação ), .\HALT_TÉRMINO (\n2_dec_1_halt_término ));
  and and_1 (and_1_out, n2_dec_1_fetch_busca, clock);
  and and_2 (and_2_out, n2_dec_1_load_leitura, clock);
  and and_3 (and_3_out, OPERACAO[0], clock);
  and and_4 (and_4_out, OPERACAO[1], clock);
  and and_5 (and_5_out, n2_dec_1_store_escrita, clock);
  and and_6 (and_6_out, \n2_dec_1_nop_sem_operação , clock);
  and and_7 (and_7_out, \n2_dec_1_halt_término , clock);
  assign controlled_buffer_1_out = and_1_out ? cont_1_valor_out : 8'bz;  // Controlled_Buffer controlled_buffer_1
  CONT cont_1 (.MINIMO({8{1'b0}}), .CLOCK(and_1_out), .VALOR_OUT(cont_1_valor_out), .MAXIMO(8'h6));
  assign controlled_buffer_1_out = and_2_out ? cont_2_valor_out : 8'bz;  // Controlled_Buffer controlled_buffer_2
  CONT cont_2 (.MINIMO(8'ha), .CLOCK(and_2_out), .VALOR_OUT(cont_2_valor_out), .MAXIMO(8'h11));
  assign controlled_buffer_1_out = and_3_out ? cont_3_valor_out : 8'bz;  // Controlled_Buffer controlled_buffer_3
  CONT cont_3 (.MINIMO(8'h15), .CLOCK(and_3_out), .VALOR_OUT(cont_3_valor_out), .MAXIMO(8'h1f));
  assign controlled_buffer_1_out = and_4_out ? cont_4_valor_out : 8'bz;  // Controlled_Buffer controlled_buffer_4
  CONT cont_4 (.MINIMO(8'h23), .CLOCK(and_4_out), .VALOR_OUT(cont_4_valor_out), .MAXIMO(8'h2a));
  assign controlled_buffer_1_out = and_5_out ? cont_5_valor_out : 8'bz;  // Controlled_Buffer controlled_buffer_5
  CONT cont_5 (.MINIMO(8'h2e), .CLOCK(and_5_out), .VALOR_OUT(cont_5_valor_out), .MAXIMO(8'h36));
  assign controlled_buffer_1_out = and_6_out ? cont_6_valor_out : 8'bz;  // Controlled_Buffer controlled_buffer_6
  CONT cont_6 (.MINIMO(8'h3a), .CLOCK(and_6_out), .VALOR_OUT(cont_6_valor_out), .MAXIMO(8'h3b));
  assign controlled_buffer_1_out = and_7_out ? cont_7_valor_out : 8'bz;  // Controlled_Buffer controlled_buffer_7
  CONT cont_7 (.MINIMO(8'h3f), .CLOCK(and_7_out), .VALOR_OUT(cont_7_valor_out), .MAXIMO(8'h3f));
  ROM #(.dataWidth(18)) rom_1 (.addr(controlled_buffer_1_out), .data(out_5));  // open: sel

  assign \ENDEREÇO  = {4'b0000, INPUT[3:0]};

  // Notes on the sheet:
  //   mínimo ->
  //   máximo ->
  //   UNIDADE DE CONTROLE
  //   MICROPROGRAMA EM MEMÓRIA ROM
  //   Intervalos em hexadecimal
  //   -> vai para a ULA
  //   01 = SOMA
  //   MEMÓRIA ROM MICROPROGRAMADA
  //   10 = COMPARAÇÃO
  //   contents of rom_1 (hex, n*v repeats v):
  //   2 1 4 10 20 40 80 0 0 0 100 4 10 20 40 2000 10000 80 0 0 0 100 4 10 20 40 200 400 1000 2000 10000 80
  //   0 0 0 100 4 8000 20 8 4000 10000 80 0 0 0 100 4 10 20 40 200 800 10000 80 0 0 80 0 10000
  //   SINAIS DE CONTROLE
endmodule
