// Logisim project 8_cpu.circ as structural Verilog: 1 circuit, main circuit main
module main (
  input  CLOCK,
  output [7:0] ACC_OUT
);

  wire CLOCK_out, n5_ula_1_a_maior_b, n5_ula_1_b_maior_a, n5_ula_1_iguais;
  wire [1:0] n6_uc_1_operacao;
  wire [7:0] n1_pc_1_contador, n5_ula_1_acc_out, \n6_uc_1_endereço , PC_BUS_out, ram_1_data, RDM_q, REM_q,
       RI_CLEAR_out, RI_q;
  wire [17:0] n6_uc_1_out_5;

  _1_pc u_1_pc_1 (.PC_TG(n6_uc_1_out_5[0]), .CONTADOR(n1_pc_1_contador));  // open: PC_CLEAR
  assign PC_BUS_out = n6_uc_1_out_5[1] ? n1_pc_1_contador : 8'bz;  // Controlled_Buffer PC_BUS
  assign PC_BUS_out = n6_uc_1_out_5[8] ? \n6_uc_1_endereço  : 8'bz;  // Controlled_Buffer UC_BUS
  assign RI_CLEAR_out = n6_uc_1_out_5[16] ? {8{1'b0}} : 8'bz;  // Controlled_Buffer RI_CLEAR
  Register RI (.D(RI_CLEAR_out), .Q(RI_q), .clk(n6_uc_1_out_5[7]));  // open: en, clr
  Clock u_CLOCK (.out(CLOCK_out));
  _6_uc u_6_uc_1 (
    .INPUT(RI_q), .\ENDEREÇO (\n6_uc_1_endereço ), .OPERACAO(n6_uc_1_operacao), .out_5(n6_uc_1_out_5),
    .clock(CLOCK_out));
  Register REM (.D(PC_BUS_out), .Q(REM_q), .clk(n6_uc_1_out_5[2]));  // open: en, clr
  _5_ula u_5_ula_1 (
    .ACC_IN(ACC_OUT), .INPUT(RI_CLEAR_out), .ACC_OUT(n5_ula_1_acc_out), .A_MAIOR_B(n5_ula_1_a_maior_b),
    .IGUAIS(n5_ula_1_iguais), .B_MAIOR_A(n5_ula_1_b_maior_a), .ULA_TG(n6_uc_1_out_5[9]),
    .OPERACAO(n6_uc_1_operacao), .ADD_TG(n6_uc_1_out_5[10]), .COMP_TG(n6_uc_1_out_5[11]));
  LED A_MAIOR_B (.in(n5_ula_1_a_maior_b));
  LED IGUAIS (.in(n5_ula_1_iguais));
  LED B_MAIOR_A (.in(n5_ula_1_b_maior_a));
  RAM ram_1 (.addr(REM_q), .data(ram_1_data), .clk(n6_uc_1_out_5[3]), .ld(n6_uc_1_out_5[4]));  // open: sel, clr
  assign RI_CLEAR_out = n6_uc_1_out_5[12] ? n5_ula_1_acc_out : 8'bz;  // Controlled_Buffer ULA_BUS
  Register RDM (.D(ram_1_data), .Q(RDM_q), .clk(n6_uc_1_out_5[5]));  // open: en, clr
  _3_acc u_3_acc_1 (.IN(RI_CLEAR_out), .ACC_TG(n6_uc_1_out_5[13]), .ACC_CLEAR(n6_uc_1_out_5[14]), .ACC_OUT(ACC_OUT));
  assign RI_CLEAR_out = n6_uc_1_out_5[6] ? RDM_q : 8'bz;  // Controlled_Buffer RDM_BUS
  assign ram_1_data = n6_uc_1_out_5[15] ? ACC_OUT : 8'bz;  // Controlled_Buffer ACC_BUS

  // Notes on the sheet:
  //   ARQUITETURA DE COMPUTADORES - CPU TOLEDO v2.0 - AUTOMÁTICA
  //   MEMÓRIA RAM
endmodule
